# Fritzing sketch 407Putt (saved by Fritzing 0.9.10b)
breadboards: 1

parts:
  Power_plug1 = Power plug
  Arduino_Uno = Arduino Uno (Rev3)
  Rx = IR break beam 3mm rx [package=THT]
  Tx = IR break beam 3mm tx [package=THT]
  Part1 = Arduino Board Ethernet
  Rx1 = IR break beam 3mm rx [package=THT]
  Rx2 = IR break beam 3mm rx [package=THT]
  Rx3 = IR break beam 3mm rx [package=THT]
  Rx4 = IR break beam 3mm rx [package=THT]
  Rx7 = IR break beam 3mm rx [package=THT]
  Rx8 = IR break beam 3mm rx [package=THT]

nets:
  GND: Power_plug1.GND, Arduino_Uno.GND, Rx.pin3, Tx.pin2, Part1.GND, Rx1.pin3, Rx2.pin3, Rx3.pin3, Rx4.pin3, Rx7.pin3, Rx8.pin3
  5V: Power_plug1.VCC, Arduino_Uno.5V, Rx.pin1, Tx.pin1, Part1.5V, Rx1.pin1, Rx2.pin1, Rx3.pin1, Rx4.pin1, Rx7.pin1, Rx8.pin1
  N1: Arduino_Uno.A0, Part1.A0
  N2: Arduino_Uno.A1, Part1.A1
  N3: Arduino_Uno.A2, Part1.A2
  N4: Arduino_Uno.A3, Part1.A3
  N5: Arduino_Uno.A4/SDA, Part1.A4
  N6: Arduino_Uno.A5/SCL, Part1.A5
  N7: Arduino_Uno.D9_PWM, Part1.D9_PWM, Rx8.pin2
  N8: Arduino_Uno.D10_PWM/SS, Part1.D10_PWM/SS
  N9: Arduino_Uno.D11_PWM/MOSI, Part1.D11/MOSI
  N10: Arduino_Uno.D12/MISO, Part1.D12/MISO
  N11: Arduino_Uno.D13/SCK, Part1.D13/SCK
  N12: Arduino_Uno.AREF, Part1.AREF
  N13: Arduino_Uno.D0/RX, Part1.D0/RX
  N14: Arduino_Uno.D1/TX, Part1.D1/TX
  N15: Arduino_Uno.D2, Rx.pin2, Part1.D2_PWM
  N16: Arduino_Uno.D3_PWM, Part1.D3_PWM, Rx1.pin2
  N17: Arduino_Uno.RESET, Part1.RESET
  3V3: Arduino_Uno.3V3, Part1.3V3
  VIN: Arduino_Uno.VIN, Part1.VIN
  N18: Part1.D8, Rx7.pin2
  N19: Part1.D5_PWM, Rx2.pin2
  N20: Part1.D6_PWM, Rx3.pin2
  N21: Part1.D7, Rx4.pin2

custom parts:
  IR break beam 3mm rx: Infrared break beam Sensor rx module.
  IR break beam 3mm tx: Infrared break beam Sensor tx module.
